# Fritzing sketch reversed brightness (saved by Fritzing 0.9.3b)
breadboards: 1

parts:
  Part1 = Arduino Uno (Rev3)
  LED1 = LED - 5mm [color="Red (633nm)" package="5 mm [THT]"]
  R1 = Resistor [tolerance=±5% resistance=220 package=THT]

nets:
  N1: Part1.D9_PWM, LED1.cathode
  N2: Part1.5V, R1.Pin_0
  N3: LED1.anode, R1.Pin_1
